// Logisim project Proyecto ALU.circ as structural Verilog: 6 circuits, main circuit main
module main (
  input  a1,
  input  a2,
  input  in_3,
  input  a3,
  input  a4,
  input  b1,
  input  b2,
  input  b3,
  input  b4
);

  wire l_7_segmentos_6324581b_1_d1, l_7_segmentos_6324581b_1_d2, l_7_segmentos_6324581b_1_d3,
       l_7_segmentos_6324581b_1_d4, l_7_segmentos_6324581b_1_d5, l_7_segmentos_6324581b_1_d6,
       l_7_segmentos_6324581b_1_d7, l_7_segmentos_6324581b_1_u1, l_7_segmentos_6324581b_1_u2,
       l_7_segmentos_6324581b_1_u3, l_7_segmentos_6324581b_1_u4, l_7_segmentos_6324581b_1_u5,
       l_7_segmentos_6324581b_1_u6, l_7_segmentos_6324581b_1_u7, suma_1_acarr, suma_1_x1, suma_1_x2,
       suma_1_x3, suma_1_x4;

  SUMA suma_1 (
    .vacio(in_3), .A1(a1), .B1(b1), .A2(a2), .B2(b2), .A3(a3), .B3(b3), .A4(a4), .B4(b4), .x1(suma_1_x1),
    .x2(suma_1_x2), .x3(suma_1_x3), .x4(suma_1_x4), .acarr(suma_1_acarr));
  L_7_SEGMENTOS_6324581b l_7_segmentos_6324581b_1 (
    .A(suma_1_acarr), .B(suma_1_x1), .C(suma_1_x2), .D(suma_1_x3), .E(suma_1_x4),
    .U1(l_7_segmentos_6324581b_1_u1), .U2(l_7_segmentos_6324581b_1_u2), .U3(l_7_segmentos_6324581b_1_u3),
    .U4(l_7_segmentos_6324581b_1_u4), .U5(l_7_segmentos_6324581b_1_u5), .U6(l_7_segmentos_6324581b_1_u6),
    .U7(l_7_segmentos_6324581b_1_u7), .D1(l_7_segmentos_6324581b_1_d1), .D2(l_7_segmentos_6324581b_1_d2),
    .D3(l_7_segmentos_6324581b_1_d3), .D4(l_7_segmentos_6324581b_1_d4), .D5(l_7_segmentos_6324581b_1_d5),
    .D6(l_7_segmentos_6324581b_1_d6), .D7(l_7_segmentos_6324581b_1_d7));
  _7_Segment_Display u_7_segment_display_1 (
    .g(l_7_segmentos_6324581b_1_d7), .f(l_7_segmentos_6324581b_1_d6), .a(l_7_segmentos_6324581b_1_d1),
    .b(l_7_segmentos_6324581b_1_d2), .e(l_7_segmentos_6324581b_1_d5), .d(l_7_segmentos_6324581b_1_d4),
    .c(l_7_segmentos_6324581b_1_d3));  // open: dp
  _7_Segment_Display u_7_segment_display_2 (
    .g(l_7_segmentos_6324581b_1_u7), .f(l_7_segmentos_6324581b_1_u6), .a(l_7_segmentos_6324581b_1_u1),
    .b(l_7_segmentos_6324581b_1_u2), .e(l_7_segmentos_6324581b_1_u5), .d(l_7_segmentos_6324581b_1_u4),
    .c(l_7_segmentos_6324581b_1_u3));  // open: dp

  // Other names for the same wires on the sheet: a = a1; b = a2; c = a3; d = a4; e = b1; f = b2; g = b3; h = b4
endmodule

module SUMA (
  input  A1,
  input  A2,
  input  A3,
  input  A4,
  input  vacio,
  input  B1,
  input  B2,
  input  B3,
  input  B4,
  output x3,
  output x4,
  output x1,
  output x2,
  output acarr
);

  wire a, b, c;

  SUMA_SIMPLE suma_simple_1 (.A(A4), .B(B4), .in_3(vacio), .X(x4), .Acarr(a));
  SUMA_SIMPLE suma_simple_2 (.A(A3), .B(B3), .in_3(a), .X(x3), .Acarr(b));
  SUMA_SIMPLE suma_simple_3 (.A(A2), .B(B2), .in_3(b), .X(x2), .Acarr(c));
  SUMA_SIMPLE suma_simple_4 (.A(A1), .B(B1), .in_3(c), .X(x1), .Acarr(acarr));
endmodule

module SUMA_SIMPLE (
  input  A,
  input  B,
  input  in_3,
  output X,
  output Acarr
);

  wire and_1_out, and_2_out, and_3_out, and_4_out, and_5_out, and_6_out, and_7_out, not_1_out, not_2_out,
       not_3_out, not_4_out, not_5_out, not_6_out;

  not not_1 (not_1_out, A);
  not not_2 (not_2_out, B);
  not not_3 (not_3_out, A);
  not not_4 (not_4_out, in_3);
  not not_5 (not_5_out, B);
  not not_6 (not_6_out, in_3);
  and and_1 (and_1_out, B, in_3);
  and and_2 (and_2_out, A, in_3);
  and and_3 (and_3_out, A, B);
  and and_4 (and_4_out, not_1_out, not_2_out, in_3);
  and and_5 (and_5_out, not_3_out, B, not_4_out);
  and and_6 (and_6_out, A, not_5_out, not_6_out);
  and and_7 (and_7_out, A, B, in_3);
  or or_1 (Acarr, and_1_out, and_2_out, and_3_out);
  or or_2 (X, and_4_out, and_5_out, and_6_out, and_7_out);
endmodule

module L_7_SEGMENTOS_6324581b (
  input  A,
  input  B,
  input  C,
  input  D,
  input  E,
  output U1,
  output U2,
  output U3,
  output U4,
  output U5,
  output U6,
  output U7,
  output D1,
  output D2,
  output D3,
  output D4,
  output D5,
  output D6,
  output D7
);

  wire and_1_out, and_2_out, and_3_out, and_4_out, and_5_out, and_6_out, and_7_out, and_8_out, and_9_out,
       and_10_out, and_11_out, and_12_out, and_13_out, and_14_out, and_15_out, and_16_out, and_17_out,
       and_18_out, and_19_out, and_20_out, and_21_out, and_22_out, and_23_out, and_24_out, and_25_out,
       and_26_out, and_27_out, and_28_out, and_29_out, and_30_out, and_31_out, and_32_out, and_33_out,
       and_34_out, and_35_out, and_36_out, and_37_out, and_38_out, and_39_out, and_40_out, and_41_out,
       and_42_out, and_43_out, and_44_out, and_45_out, and_46_out, and_47_out, and_48_out, and_49_out,
       and_50_out, and_51_out, and_52_out, and_53_out, and_54_out, and_55_out, and_56_out, and_57_out,
       and_58_out, and_59_out, and_60_out, and_61_out, and_62_out, and_63_out, and_64_out, and_65_out,
       and_66_out, and_67_out, and_68_out, and_69_out, and_70_out, and_71_out, and_72_out, and_73_out,
       and_74_out, and_75_out, not_1_out, not_2_out, not_3_out, not_4_out, not_5_out;

  not not_1 (not_1_out, A);
  not not_2 (not_2_out, B);
  not not_3 (not_3_out, C);
  not not_4 (not_4_out, D);
  not not_5 (not_5_out, E);
  and and_1 (and_1_out, not_1_out, not_3_out, not_5_out);
  and and_2 (and_2_out, not_2_out, D);
  and and_3 (and_3_out, not_1_out, C, E);
  and and_4 (and_4_out, not_1_out, B, not_4_out);
  and and_5 (and_5_out, B, C, not_4_out);
  and and_6 (and_6_out, A, not_2_out, not_5_out);
  and and_7 (and_7_out, A, not_3_out, E);
  and and_8 (and_8_out, A, D, not_5_out);
  and and_9 (and_9_out, not_1_out, not_3_out);
  and and_10 (and_10_out, not_1_out, not_4_out, not_5_out);
  and and_11 (and_11_out, not_2_out, not_3_out, E);
  and and_12 (and_12_out, not_2_out, not_3_out, D);
  and and_13 (and_13_out, not_2_out, D, E);
  and and_14 (and_14_out, not_3_out, D, E);
  and and_15 (and_15_out, B, not_4_out, not_5_out);
  and and_16 (and_16_out, B, C, not_4_out);
  and and_17 (and_17_out, B, C, not_5_out);
  and and_18 (and_18_out, A, not_2_out, C);
  and and_19 (and_19_out, not_2_out, not_4_out);
  and and_20 (and_20_out, not_3_out, not_4_out);
  and and_21 (and_21_out, not_1_out, not_2_out, C);
  and and_22 (and_22_out, B, D);
  and and_23 (and_23_out, A, not_3_out);
  and and_24 (and_24_out, A, not_4_out);
  and and_25 (and_25_out, not_1_out, not_3_out, not_5_out);
  and and_26 (and_26_out, not_2_out, not_3_out, not_5_out);
  and and_27 (and_27_out, not_2_out, not_3_out, D);
  and and_28 (and_28_out, not_2_out, D, not_5_out);
  and and_29 (and_29_out, not_3_out, D, not_5_out);
  and and_30 (and_30_out, not_1_out, C, not_4_out, E);
  and and_31 (and_31_out, not_1_out, B, not_4_out);
  and and_32 (and_32_out, B, not_4_out, E);
  and and_33 (and_33_out, B, C, E);
  and and_34 (and_34_out, A, not_2_out, D);
  and and_35 (and_35_out, A, C, not_5_out);
  and and_36 (and_36_out, not_1_out, not_3_out, not_5_out);
  and and_37 (and_37_out, not_2_out, not_3_out, not_5_out);
  and and_38 (and_38_out, not_2_out, D, not_5_out);
  and and_39 (and_39_out, not_3_out, D, not_5_out);
  and and_40 (and_40_out, not_1_out, B, not_4_out, not_5_out);
  and and_41 (and_41_out, A, C, not_5_out);
  and and_42 (and_42_out, not_2_out, not_4_out, not_5_out);
  and and_43 (and_43_out, not_1_out, not_2_out, C, not_4_out);
  and and_44 (and_44_out, not_1_out, not_2_out, C, not_5_out);
  and and_45 (and_45_out, B, not_3_out, not_4_out);
  and and_46 (and_46_out, B, D, not_5_out);
  and and_47 (and_47_out, not_1_out, B, C, D);
  and and_48 (and_48_out, A, not_2_out, not_3_out, D);
  and and_49 (and_49_out, A, B, not_4_out);
  and and_50 (and_50_out, not_2_out, not_3_out, D);
  and and_51 (and_51_out, not_2_out, D, not_5_out);
  and and_52 (and_52_out, not_1_out, C, not_4_out);
  and and_53 (and_53_out, B, not_4_out);
  and and_54 (and_54_out, not_1_out, B, C);
  and and_55 (and_55_out, A, not_3_out, not_5_out);
  and and_56 (and_56_out, A, not_2_out, D);
  and and_57 (and_57_out, not_1_out, not_2_out);
  and and_58 (and_58_out, A, B);
  and and_59 (and_59_out, not_1_out, not_3_out, not_4_out);
  and and_60 (and_60_out, A, C);
  and and_61 (and_61_out, not_2_out, not_3_out);
  and and_62 (and_62_out, B, C, D);
  and and_63 (and_63_out, not_1_out, not_2_out);
  and and_64 (and_64_out, A, B);
  and and_65 (and_65_out, not_1_out, not_3_out, not_4_out);
  and and_66 (and_66_out, A, C);
  and and_67 (and_67_out, not_1_out, not_2_out);
  and and_68 (and_68_out, not_2_out, C);
  and and_69 (and_69_out, A, B, not_3_out);
  and and_70 (and_70_out, not_1_out, not_3_out, not_4_out);
  and and_71 (and_71_out, A, C, not_4_out);
  and and_72 (and_72_out, not_1_out, not_2_out);
  and and_73 (and_73_out, not_1_out, not_3_out, not_4_out);
  and and_74 (and_74_out, A, C);
  and and_75 (and_75_out, A, B);
  or or_1 (U1, and_1_out, and_2_out, and_3_out, and_4_out, and_5_out, and_6_out, and_7_out, and_8_out);
  or or_2 (U2, and_9_out, and_10_out, and_11_out, and_12_out, and_13_out, and_14_out, and_15_out, and_16_out, and_17_out, and_18_out);
  or or_3 (U3, and_19_out, and_20_out, E, and_21_out, and_22_out, and_23_out, and_24_out);
  or or_4 (U4, and_25_out, and_26_out, and_27_out, and_28_out, and_29_out, and_30_out, and_31_out, and_32_out, and_33_out, and_34_out, and_35_out);
  or or_5 (U5, and_36_out, and_37_out, and_38_out, and_39_out, and_40_out, and_41_out);
  or or_6 (U6, and_42_out, and_43_out, and_44_out, and_45_out, and_46_out, and_47_out, and_48_out, and_49_out);
  or or_7 (U7, and_50_out, and_51_out, and_52_out, and_53_out, and_54_out, and_55_out, and_56_out);
  or or_8 (D1, and_57_out, and_58_out, and_59_out, and_60_out);
  or or_9 (D3, not_1_out, and_61_out, and_62_out);
  or or_10 (D4, and_63_out, and_64_out, and_65_out, and_66_out);
  or or_11 (D5, and_67_out, and_68_out, and_69_out, and_70_out, and_71_out);
  or or_12 (D6, and_72_out, and_73_out);
  or or_13 (D7, and_74_out, and_75_out);

  assign D2 = 1'b1;
endmodule

module RESTA_SIMPLE (
  input  a,
  input  b,
  input  SIG,
  output x
);

  wire and_1_out, and_2_out, not_1_out, not_2_out;

  not not_1 (not_1_out, a);
  not not_2 (not_2_out, b);
  and and_1 (and_1_out, not_1_out, b, SIG);
  and and_2 (and_2_out, a, not_2_out);
  or or_1 (x, and_1_out, and_2_out);
endmodule

module RESTA (
  input  A1,
  input  A2,
  input  A3,
  input  A4,
  input  B1,
  input  B2,
  input  B3,
  input  B4,
  input  in_9,
  output out_10,
  output out_11,
  output out_12,
  output out_13
);

  RESTA_SIMPLE resta_simple_1 (.a(A4), .b(B4), .SIG(A3), .x(out_11));
  RESTA_SIMPLE resta_simple_2 (.a(A3), .b(B3), .SIG(A2), .x(out_10));
  RESTA_SIMPLE resta_simple_3 (.a(A2), .b(B2), .SIG(A1), .x(out_13));
  RESTA_SIMPLE resta_simple_4 (.a(A1), .b(B1), .SIG(in_9), .x(out_12));
endmodule
